# Fritzing sketch balloon (saved by Fritzing 0.8.0b)

parts:
  Part3 = Radiometrix NTX2
  Part4 = Assembled uBLOX MAX-6 Pico Breakout with Chip Scale Antenna
  R1 = Resistor [tolerance=±5% resistance=4.7k package=THT]
  R2 = Resistor [tolerance=±5% resistance=4.7k package=THT]
  R3 = Resistor [tolerance=±5% resistance=4.7k package=THT]
  U1 = Voltage Regulator - 3.3V [package="TO220 [THT]"]
  Raspberry_Pi2 = Raspberry Pi
  ANT1 = Antenna
  Part5 = Barometric Pressure Sensor - BMP085 Breakout
  VCC3 = 4 x AAA Battery Mount
  C3 = Ceramic Capacitor [capacitance="100 nF" package="0603 [SMD, multilayer]"]

nets:
  N1: Part3.RF_out, ANT1.antenna_lead
  VCC: Part3.En, Part3.Vcc, Part4.VCC, R2.Pin_1, Raspberry_Pi2.3V3, Part5.VCC, C3.0
  N2: Part3.0V, R1.Pin_0, Raspberry_Pi2.Pin_9_DNC
  N3: Part3.TXD, R1.Pin_1, R2.Pin_0, R3.Pin_0
  N4: Part4.SDA, Raspberry_Pi2.I2C_SDA0, Part5.SDA
  N5: Part4.SCL, Raspberry_Pi2.I2C_SCL_0, Part5.SCL
  GND: Part4.GND, Raspberry_Pi2.GND, Part5.GND, C3.1
  N6: R3.Pin_1, Raspberry_Pi2.GPIO3
  N7: U1.input_voltage, VCC3.+
  N8: U1.GND, Raspberry_Pi2.GND_(RG2)
  N9: U1.output_voltage, Raspberry_Pi2.Vcc_OUT_(RG2), Raspberry_Pi2.Vcc_IN_(RG2)
  N10: Raspberry_Pi2.GND_(TP2), VCC3.-

custom parts:
  Radiometrix NTX2: The NTX2 transmitter and NRX2 receiver offer a low power, reliable data link in a Radiometrix SIL standard pin out and foot print.
  Assembled uBLOX MAX-6 Pico Breakout with Chip Scale Antenna: The board is assembled with a uBLOX MAX-6 module, chip scale antenna and a decoupling capacitor. This board has VCC, GND and RX & TX, SCL & SDA for I2C. MAX comes in an ultra-compact, easy-to-mount 9.7mm x 10.1mm LCC package, and supports temperatures down to -40'C. Supports temperatures down to -40'C UART interface. RTC crystal for faster warm and hot starts Suitable for HAB Usage Max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
  Raspberry Pi: The awesome Raspberry Pi ARM Board
